# Fritzing sketch Servo_knob (saved by Fritzing 0.9.3b)
breadboards: 1

parts:
  Part1 = Arduino Uno (Rev3)
  J1 = Basic Servo
  R1 = Rotary Potentiometer (Small) [maximum_resistance=100kΩ package=THT]

nets:
  N1: Part1.A3, R1.wiper
  N2: Part1.D13/SCK, J1.pulse
  N3: Part1.3V3, R1.leg1
  5V: Part1.5V, J1.vcc
  GND: Part1.GND, J1.gnd, R1.leg2
