# Fritzing sketch stepper_demo (saved by Fritzing 0.9.3b)
breadboards: 1

parts:
  Part1 = Arduino Uno (Rev3)
  Pololu_A1 = Pololu A4988 [package=SO16]
  JACK1 = 2.1mm Barrel Jack with Terminal Block
  C1 = Capacitor Polarized [package=cpol-radial-100uf-25v]
  M1 = Stepper Motor - Bipolar

nets:
  N1: Part1.D8, Pololu_A1.DIR
  N2: Part1.D9_PWM, Pololu_A1.STEP
  N3: Part1.D10_PWM/SS, Pololu_A1.MS3
  N4: Part1.D11_PWM/MOSI, Pololu_A1.MS2
  N5: Part1.D12/MISO, Pololu_A1.MS1
  3V3: Part1.3V3, Pololu_A1.VDD
  N6: Part1.GND, Pololu_A1.GND#8
  N7: Pololu_A1.RESET, Pololu_A1.SLEEP
  N8: Pololu_A1.1B, M1.D
  N9: Pololu_A1.1A, M1.B
  N10: Pololu_A1.2A, M1.C
  N11: Pololu_A1.2B, M1.A
  N12: Pololu_A1.GND#14, JACK1.NEG, C1.-
  N13: Pololu_A1.VMOT, JACK1.POS, C1.+
