# Fritzing sketch IOT_demo_6 (saved by Fritzing 0.9.3b)
breadboards: 1

parts:
  Part1 = Arduino Uno (Rev3) - ICSP
  Part2 = Adafruit DRV8833 DC/Stepper Motor Driver [part_number="Adafruit #3297"]
  M1 = DC Motor [part_number=Left]
  M2 = DC Motor [part_number=Right]
  SG1 = Buzzer 12mm [part_number=Buzzer package=buzzer-12mm-ns]
  S1 = Pushbutton [part_number=Sleep package="[THT]"]
  R1 = Resistor [tolerance=±5% resistance=10k package=THT]

nets:
  N1: Part1.ICSP_MISO, Part1.D12/MISO, Part2.AIN1
  N2: Part1.D8, SG1.1
  N3: Part1.D13/SCK, Part2.AIN2
  N4: Part1.D3_PWM, S1.Pin_1, S1.Pin_2
  N5: Part1.D4, Part2.BIN2
  N6: Part1.D5_PWM, Part2.BIN1
  N7: Part1.D6_PWM, Part2.!SLEEP
  N8: Part1.5V, Part2.VMOTOR
  GND: Part1.GND, Part2.GND, SG1.2, R1.Pin_0
  N9: Part2.AOUT1, M2.pin_2
  N10: Part2.BOUT1, M1.pin_1
  N11: Part2.BOUT2, M1.pin_2
  N12: S1.Pin_3, S1.Pin_4, R1.Pin_1

custom parts:
  Adafruit DRV8833 DC/Stepper Motor Driver: Spin two DC motors or step one bi-polar or uni-polar stepper with up to 1.2A per channel using the DRV8833. This motor driver chip is a nice alternative to the TB6612 driver. Like that chip, you get 2 full H-bridges, but this chip is better for low voltage uses (can run from 2.7V up to 10.8V motor power) and has built in current limiting capability. We set it up for 1A current limiting so you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
